# Fritzing sketch schematik (saved by Fritzing 0.9.3b)

parts:
  Part1 = Arduino Uno (Rev3)
  U1 = NodeMCU V3.0
  OLED1 = OLED 128x64 I2C Monochrome Display
  hc-sr1 = hc-sr04  # not connected
  SP1 = SPEAKER [package=pcb_mount_speaker]  # not connected

nets:
  GND: Part1.GND, U1.GND, OLED1.GND
  N1: U1.D1, OLED1.SCK
  N2: U1.D2, OLED1.SDA
  3V3: U1.3V3, OLED1.VDD

custom parts:
  NodeMCU V3.0: ESP8266 based NodeMCU
